// Logisim project address_decode.circ as structural Verilog: 1 circuit, main circuit main
module main (
);

  wire A0, A1, A2, A3, A4, A5, A6, A7, A8, A9, A10, A11, A12, A13, A13OR12, A14, A15, and_1_out, and_2_out,
       and_3_out, and_4_out, and_5_out, and_6_out, and_7_out, and_8_out, and_9_out, and_10_out, and_11_out,
       and_12_out, B2, BB, BRR, BRW, nand_1_out, nand_2_out, nand_3_out, not_1_out, not_2_out, not_3_out,
       not_4_out, or_1_out, or_3_out, or_4_out, or_5_out, or_6_out, RW;

  Hex_Digit_Display hex_digit_display_1 (.value({A15, A14, A13, A12}));  // open: dp
  DipSwitch #(.number(16)) dipswitch_1 (
    .sw1(A15), .sw2(A14), .sw3(A13), .sw4(A12), .sw5(A11), .sw6(A10), .sw7(A9), .sw8(A8), .sw9(A7),
    .sw10(A6), .sw11(A5), .sw12(A4), .sw13(A3), .sw14(A2), .sw15(A1), .sw16(A0));
  Hex_Digit_Display hex_digit_display_2 (.value({A11, A10, A9, A8}));  // open: dp
  Hex_Digit_Display hex_digit_display_3 (.value({A7, A6, A5, A4}));  // open: dp
  Hex_Digit_Display hex_digit_display_4 (.value({A3, A2, A1, A0}));  // open: dp
  DipSwitch #(.number(5)) dipswitch_2 (.sw1(BB), .sw2(B2), .sw3(BRW), .sw4(BRR), .sw5(RW));
  LED dev (.in(or_1_out));
  or or_1 (or_1_out, nand_2_out, or_3_out);
  or or_2 (A13OR12, A13, A12);
  or or_3 (or_3_out, A13OR12, A11);
  LED ram (.in(nand_1_out));
  nand nand_1 (nand_1_out, or_1_out, and_1_out);
  nand nand_2 (nand_2_out, A14, A15);
  LED rom (.in(and_1_out));
  and and_1 (and_1_out, or_4_out, nand_3_out);
  or or_4 (or_4_out, or_5_out, or_6_out);
  or or_5 (or_5_out, nand_2_out, and_2_out);
  and and_2 (and_2_out, not_2_out, not_1_out);
  not not_1 (not_1_out, A13);
  not not_2 (not_2_out, A12);
  nand nand_3 (nand_3_out, and_3_out, not_3_out);
  and and_3 (and_3_out, and_4_out, BB);
  and and_4 (and_4_out, A13OR12, A15);
  not not_3 (not_3_out, A14);
  or or_6 (or_6_out, and_5_out, and_8_out);
  and and_5 (and_5_out, BRR, RW);
  LED A16 (.in(and_6_out));
  and and_6 (and_6_out, and_7_out, and_9_out);
  and and_7 (and_7_out, or_6_out, B2);
  and and_8 (and_8_out, BRW, not_4_out);
  not not_4 (not_4_out, RW);
  and and_9 (and_9_out, A12, and_11_out);
  and and_10 (and_10_out, not_1_out, A14);
  and and_11 (and_11_out, and_10_out, and_12_out);
  and and_12 (and_12_out, A14, A15);
endmodule
